// Logisim project RSC.circ as structural Verilog: 10 circuits, main circuit Arith_U
// AU
module Arith_U (
  input  [31:0] A,
  input  [31:0] B,
  input  S1,
  input  S0,
  output [31:0] AU_out
);

  wire and_1_out, xnor_1_out;
  wire [31:0] adder_1_out, multiplexer_1_out, not_1_out;

  assign not_1_out = ~B;  // NOT_Gate not_1, 32 bits wide
  xnor xnor_1 (xnor_1_out, S0, S1);
  Adder #(.width(32)) adder_1 (.a(A), .b(multiplexer_1_out), .out(adder_1_out), .cin(xnor_1_out));  // open: cout
  Multiplexer #(.select(2), .width(32), .enable("false")) multiplexer_1 (
    .in0(not_1_out), .in1(B), .in2(32'h1), .in3(B), .out(multiplexer_1_out), .sel({S1, S0}));
  and and_1 (and_1_out, S0, S1);
  Multiplexer #(.width(32), .enable("false")) multiplexer_2 (
    .in0(adder_1_out), .in1(multiplexer_1_out), .out(AU_out), .sel(and_1_out));

  // Notes on the sheet:
  //   CLA 4
  //   Arithmetic Unit
  //   PUJAN NEPAL AND DIWAS DULAL
endmodule

// Lu
module Logic_U (
  input  [31:0] A,
  input  S1,
  input  S0,
  input  [31:0] B,
  output [31:0] Logic_Out
);

  wire [31:0] and_1_out, not_1_out, or_1_out, shifter_1_out;

  // Probe on A
  // Probe on B
  assign not_1_out = ~A;  // NOT_Gate not_1, 32 bits wide
  assign and_1_out = A & B;  // AND_Gate and_1, 32 bits wide
  assign or_1_out = A | B;  // OR_Gate or_1, 32 bits wide
  Shifter #(.width(32), .shift("ar")) shifter_1 (.in(A), .\dist (5'b00001), .out(shifter_1_out));
  Multiplexer #(.select(2), .width(32), .enable("false")) multiplexer_1 (
    .in0(and_1_out), .in1(or_1_out), .in2(shifter_1_out), .in3(not_1_out), .out(Logic_Out), .sel({S1, S0}));
  // Probe on Logic_Out

  // Notes on the sheet:
  //   CLA 5
  //   Logic Unit
  //   PUJAN NEPAL AND DIWAS DULAL
endmodule

module ALU (
  input  [31:0] A,
  input  [31:0] B,
  input  S2,
  input  S1,
  input  S0,
  output [31:0] ALU_OUT
);

  wire [31:0] arith_u_1_au_out, logic_u_1_logic_out;

  // Probe on A
  // Probe on B
  Arith_U arith_u_1 (.A(A), .B(B), .S1(S1), .S0(S0), .AU_out(arith_u_1_au_out));
  Logic_U logic_u_1 (.A(A), .B(B), .S1(S1), .S0(S0), .Logic_Out(logic_u_1_logic_out));
  Multiplexer #(.width(32), .enable("false")) multiplexer_1 (
    .in0(arith_u_1_au_out), .in1(logic_u_1_logic_out), .out(ALU_OUT), .sel(S2));
  // Probe on ALU_OUT

  // Notes on the sheet:
  //   CLA 5
  //   Arithmetic Unit
  //   PUJAN NEPAL AND DIWAS DULAL
endmodule

module SC (
  input  clock,
  input  Clear,
  output [2:0] SEQ_out
);

  wire [2:0] adder_1_out;

  Adder #(.width(3)) adder_1 (.a(SEQ_out), .b(3'b001), .out(adder_1_out));  // open: cin, cout
  Register #(.width(3)) register_1 (.D(adder_1_out), .Q(SEQ_out), .clk(clock), .clr(Clear));  // open: en

  // Notes on the sheet:
  //   CLA 6
  //   Sequence Counter
  //   PUJAN NEPAL AND DIWAS DULAL
endmodule

module RSC (
);

  wire control_1_acc_bus, control_1_acc_clr, control_1_acc_ld, control_1_ar_ld, control_1_dr_bus,
       control_1_dr_ld, control_1_ir_ld, control_1_outr_ld, control_1_pc_bus, control_1_pc_inc,
       control_1_pc_ld, control_1_r_bus, control_1_r_ld, control_1_ram_en, control_1_ram_r_prime_w,
       control_1_z_ld, Primary_Clock_out, z_reg_1_z_out;
  wire [2:0] control_1_alu_s;
  wire [3:0] outr_1_data_out_2, outr_1_data_out_3, outr_1_data_out_4;
  wire [31:0] acc_1_data_out, alu_1_alu_out, ar_1_data_out, dr_1_data_out, ir_1_data_out, outr_1_data_out,
       r_1_bus_out;

  Clock Primary_Clock (.out(Primary_Clock_out));
  R r_1 (
    .Data_in(r_1_bus_out), .clock(Primary_Clock_out), .Load(control_1_r_ld), .bus(control_1_r_bus),
    .Bus_out(r_1_bus_out));  // open: Data_out
  AR ar_1 (.Data_in(r_1_bus_out), .clock(Primary_Clock_out), .Load(control_1_ar_ld), .Data_out(ar_1_data_out));
  DR dr_1 (
    .Data_in(r_1_bus_out), .clock(Primary_Clock_out), .Load(control_1_dr_ld), .bus(control_1_dr_bus),
    .Data_out(dr_1_data_out), .Bus_out(r_1_bus_out));
  ALU alu_1 (
    .A(acc_1_data_out), .B(r_1_bus_out), .S2(control_1_alu_s[2]), .S1(control_1_alu_s[1]),
    .S0(control_1_alu_s[0]), .ALU_OUT(alu_1_alu_out));
  ACC acc_1 (
    .Data_in(alu_1_alu_out), .clock(Primary_Clock_out), .Load(control_1_acc_ld), .clear(control_1_acc_clr),
    .bus(control_1_acc_bus), .Data_out(acc_1_data_out), .Bus_out(r_1_bus_out));
  RAM #(.addrWidth(16), .dataWidth(32)) ram_1 (
    .addr(ar_1_data_out[15:0]), .data(r_1_bus_out), .sel(control_1_ram_en), .clk(Primary_Clock_out),
    .ld(control_1_ram_r_prime_w));  // open: clr
  PC pc_1 (
    .Data_in(r_1_bus_out), .clock(Primary_Clock_out), .count(control_1_pc_inc), .Load(control_1_pc_ld),
    .bus(control_1_pc_bus), .Bus_out(r_1_bus_out));  // open: Data_out
  IR ir_1 (.Data_in(dr_1_data_out), .clock(Primary_Clock_out), .Load(control_1_ir_ld), .Data_out(ir_1_data_out));
  Control control_1 (
    .RAM_R_prime_W(control_1_ram_r_prime_w), .RAM_EN(control_1_ram_en), .AR_LD(control_1_ar_ld),
    .PC_BUS(control_1_pc_bus), .PC_INC(control_1_pc_inc), .PC_LD(control_1_pc_ld), .DR_BUS(control_1_dr_bus),
    .DR_LD(control_1_dr_ld), .R_BUS(control_1_r_bus), .R_LD(control_1_r_ld), .ACC_BUS(control_1_acc_bus),
    .ACC_CLR(control_1_acc_clr), .ACC_LD(control_1_acc_ld), .ALU_S(control_1_alu_s),
    .OUTR_LD(control_1_outr_ld), .Z_LD(control_1_z_ld), .IR_LD(control_1_ir_ld), .Clock(Primary_Clock_out),
    .Z_In(z_reg_1_z_out), .IR_In(ir_1_data_out));  // open: T, D
  Z_Reg z_reg_1 (.ACC_in(acc_1_data_out), .Clock(Primary_Clock_out), .Load(control_1_z_ld), .Z_out(z_reg_1_z_out));
  OUTR outr_1 (
    .Data_in(r_1_bus_out), .clock(Primary_Clock_out), .Load(control_1_outr_ld),
    .Data_out({outr_1_data_out[31:16], outr_1_data_out_4, outr_1_data_out_3, outr_1_data_out_2, outr_1_data_out[3:0]}));
  Hex_Digit_Display hex_digit_display_1 (.value(outr_1_data_out[31:28]));  // open: dp
  Hex_Digit_Display hex_digit_display_2 (.value(outr_1_data_out[23:20]));  // open: dp
  Hex_Digit_Display hex_digit_display_3 (.value(outr_1_data_out[27:24]));  // open: dp
  Hex_Digit_Display hex_digit_display_4 (.value(outr_1_data_out[19:16]));  // open: dp
  Hex_Digit_Display hex_digit_display_5 (.value(outr_1_data_out_4));  // open: dp
  Hex_Digit_Display hex_digit_display_6 (.value(outr_1_data_out_2));  // open: dp
  Hex_Digit_Display hex_digit_display_7 (.value(outr_1_data_out_3));  // open: dp
  Hex_Digit_Display hex_digit_display_8 (.value(outr_1_data_out[3:0]));  // open: dp

  // Notes on the sheet:
  //   Pujan Nepal and Diwas Dulal
  //   OLA 6
  //   RSC
endmodule

module Decoder (
  input  [31:0] IR_in,
  output [15:0] D_Out,
  output [3:0] Debug_Instruction
);

  wire or_1_out;
  wire [3:0] or_2_out;
  wire [15:0] decoder_1_out0;

  Multiplexer #(.width(16), .enable("false")) multiplexer_1 (
    .in0(decoder_1_out0), .in1({16{1'b0}}), .out(D_Out), .sel(or_1_out));
  or or_1 (or_1_out, or_2_out[0], or_2_out[1], or_2_out[2], or_2_out[3]);
  assign or_2_out = IR_in[7:4] | IR_in[11:8] | IR_in[15:12] | IR_in[19:16] | IR_in[23:20] | IR_in[27:24] | IR_in[31:28];  // OR_Gate or_2, 4 bits wide
  Decoder_part #(.select(4), .enable("false")) decoder_1 (
    .out0(decoder_1_out0[0]), .out1(decoder_1_out0[1]), .out2(decoder_1_out0[2]), .out3(decoder_1_out0[3]),
    .out4(decoder_1_out0[4]), .out5(decoder_1_out0[5]), .out6(decoder_1_out0[6]), .out7(decoder_1_out0[7]),
    .out8(decoder_1_out0[8]), .out9(decoder_1_out0[9]), .out10(decoder_1_out0[10]),
    .out11(decoder_1_out0[11]), .out12(decoder_1_out0[12]), .out13(decoder_1_out0[13]),
    .out14(decoder_1_out0[14]), .out15(decoder_1_out0[15]), .sel(IR_in[3:0]));

  assign Debug_Instruction = IR_in[3:0];

  // Notes on the sheet:
  //   CLA 7
  //   Decoder
  //   Diwas Dulal and Pujan Nepal
endmodule

module Timer (
  input  Clock,
  input  Clear,
  input  Stop,
  output [7:0] T_Out
);

  wire [2:0] sc_1_seq_out;
  wire [7:0] decoder_1_out0;

  Multiplexer #(.width(8), .enable("false")) multiplexer_1 (
    .in0(decoder_1_out0), .in1({8{1'b0}}), .out(T_Out), .sel(Stop));
  Decoder_part #(.select(3), .enable("false")) decoder_1 (
    .out0(decoder_1_out0[0]), .out1(decoder_1_out0[1]), .out2(decoder_1_out0[2]), .out3(decoder_1_out0[3]),
    .out4(decoder_1_out0[4]), .out5(decoder_1_out0[5]), .out6(decoder_1_out0[6]), .out7(decoder_1_out0[7]),
    .sel(sc_1_seq_out));
  SC sc_1 (.clock(Clock), .Clear(Clear), .SEQ_out(sc_1_seq_out));

  // Notes on the sheet:
  //   CLA 7
  //   Timer
  //   Diwas Dulal and Pujan Nepal
endmodule

// Z
module Z_Reg (
  input  Clock,
  input  [31:0] ACC_in,
  input  Load,
  output Z_out
);

  wire not_1_out, or_2_out;
  wire [3:0] or_1_out;

  assign or_1_out = ACC_in[3:0] | ACC_in[7:4] | ACC_in[11:8] | ACC_in[15:12] | ACC_in[19:16] | ACC_in[23:20] | ACC_in[27:24] | ACC_in[31:28];  // OR_Gate or_1, 4 bits wide
  or or_2 (or_2_out, or_1_out[0], or_1_out[1], or_1_out[2], or_1_out[3]);
  not not_1 (not_1_out, or_2_out);
  _1bit_reg u_1bit_reg_1 (.Data(not_1_out), .Clock(Clock), .Load(Load), .Data_out(Z_out));  // open: Clear

  // Notes on the sheet:
  //   OLA 7
  //   Z_Reg
  //   Diwas Dulal and Pujan Nepal
endmodule

// control
module Control (
  input  Clock,
  input  [7:0] T,
  input  [31:0] IR_In,
  input  [3:0] D,
  input  Z_In,
  output IR_LD,
  output RAM_R_prime_W,
  output RAM_EN,
  output AR_LD,
  output PC_BUS,
  output PC_INC,
  output PC_LD,
  output DR_BUS,
  output DR_LD,
  output R_BUS,
  output R_LD,
  output ACC_BUS,
  output ACC_CLR,
  output ACC_LD,
  output [2:0] ALU_S,
  output OUTR_LD,
  output Z_LD
);

  wire n1bit_reg_1_data_out;
  wire [7:0] timer_1_t_out;
  wire [15:0] decoder_1_d_out;

  IR_LD ir_ld_1 (.t2(timer_1_t_out[2]), .clock(Clock), .IR_LD(IR_LD));
  RAM_RW ram_rw_1 (
    .t1(timer_1_t_out[1]), .t3(timer_1_t_out[3]), .t5(timer_1_t_out[5]), .d1(decoder_1_d_out[1]),
    .d2(decoder_1_d_out[2]), .d5(decoder_1_d_out[5]), .d6(decoder_1_d_out[6]), .z(Z_In),
    .RAM_RW(RAM_R_prime_W));
  RAM_EN ram_en_1 (
    .t1(timer_1_t_out[1]), .t3(timer_1_t_out[3]), .t5(timer_1_t_out[5]), .t6(timer_1_t_out[6]),
    .d1(decoder_1_d_out[1]), .d2(decoder_1_d_out[2]), .d5(decoder_1_d_out[5]), .d6(decoder_1_d_out[6]),
    .z(Z_In), .RAM_EN(RAM_EN));
  AR_LD ar_ld_1 (
    .t0(timer_1_t_out[0]), .t2(timer_1_t_out[2]), .t4(timer_1_t_out[4]), .clock(Clock),
    .d1(decoder_1_d_out[1]), .d2(decoder_1_d_out[2]), .AR_LD(AR_LD));
  PC_BUS pc_bus_1 (.t0(timer_1_t_out[0]), .t2(timer_1_t_out[2]), .PC_BUS(PC_BUS));
  PC_INC pc_inc_1 (
    .t1(timer_1_t_out[1]), .t3(timer_1_t_out[3]), .clock(Clock), .d1(decoder_1_d_out[1]),
    .d2(decoder_1_d_out[2]), .d6(decoder_1_d_out[6]), .z(Z_In), .PC_INC(PC_INC));
  PC_LD pc_ld_1 (
    .t4(timer_1_t_out[4]), .clock(Clock), .d5(decoder_1_d_out[5]), .d6(decoder_1_d_out[6]), .z(Z_In),
    .PC_LD(PC_LD));
  DR_BUS dr_bus_1 (
    .t4(timer_1_t_out[4]), .t6(timer_1_t_out[6]), .d1(decoder_1_d_out[1]), .d2(decoder_1_d_out[2]),
    .d5(decoder_1_d_out[5]), .d6(decoder_1_d_out[6]), .z(Z_In), .DR_BUS(DR_BUS));
  DR_LD dr_ld_1 (
    .t1(timer_1_t_out[1]), .t3(timer_1_t_out[3]), .t5(timer_1_t_out[5]), .clock(Clock),
    .d1(decoder_1_d_out[1]), .d2(decoder_1_d_out[2]), .d5(decoder_1_d_out[5]), .d6(decoder_1_d_out[6]),
    .z(Z_In), .DR_LD(DR_LD));
  R_BUS r_bus_1 (
    .t3(timer_1_t_out[3]), .d4(decoder_1_d_out[4]), .d8(decoder_1_d_out[8]), .d9(decoder_1_d_out[9]),
    .d12(decoder_1_d_out[12]), .d13(decoder_1_d_out[13]), .R_BUS(R_BUS));
  R_LD r_ld_1 (.t3(timer_1_t_out[3]), .clock(Clock), .d3(decoder_1_d_out[3]), .R_LD(R_LD));
  ACC_BUS acc_bus_1 (
    .t3(timer_1_t_out[3]), .t5(timer_1_t_out[5]), .d2(decoder_1_d_out[2]), .d3(decoder_1_d_out[3]),
    .d7(decoder_1_d_out[7]), .ACC_BUS(ACC_BUS));
  ACC_CLR acc_clr_1 (.t3(timer_1_t_out[3]), .d11(decoder_1_d_out[11]), .ACC_CLR(ACC_CLR));
  ACC_LD acc_ld_1 (
    .t3(timer_1_t_out[3]), .t6(timer_1_t_out[6]), .clock(Clock), .d1(decoder_1_d_out[1]),
    .d4(decoder_1_d_out[4]), .d8(decoder_1_d_out[8]), .d9(decoder_1_d_out[9]), .d10(decoder_1_d_out[10]),
    .d12(decoder_1_d_out[12]), .d13(decoder_1_d_out[13]), .d14(decoder_1_d_out[14]),
    .d15(decoder_1_d_out[15]), .ACC_LD(ACC_LD));
  ALU_SEL alu_sel_1 (
    .d1(decoder_1_d_out[1]), .d4(decoder_1_d_out[4]), .d8(decoder_1_d_out[8]), .d9(decoder_1_d_out[9]),
    .d10(decoder_1_d_out[10]), .d12(decoder_1_d_out[12]), .d13(decoder_1_d_out[13]),
    .d14(decoder_1_d_out[14]), .d15(decoder_1_d_out[15]), .s2(ALU_S[2]), .s1(ALU_S[1]), .s0(ALU_S[0]));
  OUTR_LD outr_ld_1 (.t3(timer_1_t_out[3]), .clock(Clock), .d7(decoder_1_d_out[7]), .OUTR_LD(OUTR_LD));
  Z_LD z_ld_1 (.Z_LD(Z_LD));
  Timer timer_1 (.T_Out(timer_1_t_out), .Clock(Clock), .Stop(n1bit_reg_1_data_out));  // open: Clear
  Decoder decoder_1 (.D_Out(decoder_1_d_out), .Debug_Instruction(D), .IR_in(IR_In));
  _1bit_reg u_1bit_reg_1 (.Data(1'b1), .Clock(Clock), .Clear(1'b0), .Data_out(n1bit_reg_1_data_out));  // open: Load

  // Notes on the sheet:
  //   OLA 7
  //   Control
  //   Diwas Dulal and Pujan Nepal
endmodule

module _1bit_reg (
  input  Clock,
  input  Data,
  input  Clear,
  input  Load,
  output Data_out
);

  wire and_1_out, and_2_out, not_1_out, not_2_out;

  and and_1 (and_1_out, Data, Load);
  not not_1 (not_1_out, Data);
  and and_2 (and_2_out, not_1_out, Load);
  J_K_Flip_Flop j_k_ff_1 (
    .J(and_1_out), .clk(Clock), .K(and_2_out), .Q(Data_out), .preset(1'b0), .en(not_2_out), .reset(Clear));  // open: Qn
  not not_2 (not_2_out, Clear);

  // Notes on the sheet:
  //   OLA 5
  //   1bit_reg
  //   Diwas Dulal and Pujan Nepal
endmodule
