// Logisim project custom_reg.circ as structural Verilog: 12 circuits, main circuit 1bit_reg
module _1bit_reg (
  input  Clock,
  input  Data,
  input  Clear,
  input  Load,
  output Data_out
);

  wire and_1_out, and_2_out, not_1_out, not_2_out;

  and and_1 (and_1_out, Data, Load);
  not not_1 (not_1_out, Data);
  and and_2 (and_2_out, not_1_out, Load);
  J_K_Flip_Flop j_k_ff_1 (
    .J(and_1_out), .clk(Clock), .K(and_2_out), .Q(Data_out), .preset(1'b0), .en(not_2_out), .reset(Clear));  // open: Qn
  not not_2 (not_2_out, Clear);

  // Notes on the sheet:
  //   OLA 5
  //   1bit_reg
  //   Diwas Dulal and Pujan Nepal
endmodule

module Register (
  input  clock,
  input  [31:0] Data_In,
  input  Load,
  output [31:0] Data_Out
);

  Register_part #(.width(32)) register_1 (.D(Data_In), .en(Load), .Q(Data_Out), .clk(clock));  // open: clr

  // Notes on the sheet:
  //   OLA 5
  //   Register
  //   Diwas Dulal and Pujan Nepal
endmodule

module BusRegister (
  input  clock,
  input  [31:0] Data_In,
  input  Load,
  input  Bus,
  output [31:0] Data_Out,
  output [31:0] Bus_Out
);

  Register_part #(.width(32)) register_1 (.D(Data_In), .en(Load), .Q(Data_Out), .clk(clock));  // open: clr
  assign Bus_Out = Bus ? Data_Out : 32'bz;  // Controlled_Buffer controlled_buffer_1

  // Notes on the sheet:
  //   OLA 5
  //   Bus Register
  //   Diwas Dulal and Pujan Nepal
endmodule

module ClearRegister (
  input  clock,
  input  [31:0] Data_In,
  input  bus,
  input  Load,
  input  clear,
  output [31:0] Data_Out,
  output [31:0] Bus_Out
);

  Register_part #(.width(32)) register_1 (.D(Data_In), .en(Load), .Q(Data_Out), .clk(clock), .clr(clear));
  assign Bus_Out = bus ? Data_Out : 32'bz;  // Controlled_Buffer controlled_buffer_1

  // Notes on the sheet:
  //   OLA 5
  //   ClearRegister
  //   Diwas Dulal and Pujan Nepal
endmodule

module CountRegister (
  input  clock,
  input  [31:0] Data_In,
  input  count,
  input  Load,
  input  bus,
  output [31:0] Data_Out,
  output [31:0] Bus_Out
);

  wire or_1_out;
  wire [31:0] adder_1_out, multiplexer_1_out;

  Adder #(.width(32)) adder_1 (.a(Data_Out), .b(32'h1), .out(adder_1_out));  // open: cin, cout
  or or_1 (or_1_out, count, Load);
  Multiplexer #(.width(32), .enable("false")) multiplexer_1 (
    .in0(Data_In), .in1(adder_1_out), .out(multiplexer_1_out), .sel(count));
  Register_part #(.width(32)) register_1 (
    .D(multiplexer_1_out), .en(or_1_out), .Q(Data_Out), .clk(clock));  // open: clr
  assign Bus_Out = bus ? Data_Out : 32'bz;  // Controlled_Buffer controlled_buffer_1

  // Notes on the sheet:
  //   OLA 5
  //   CountRegister
  //   Diwas Dulal and Pujan Nepal
endmodule

module ACC (
  input  clock,
  input  [31:0] Data_in,
  input  clear,
  input  Load,
  input  bus,
  output [31:0] Data_out,
  output [31:0] Bus_out
);

  ClearRegister clearregister_1 (
    .Data_In(Data_in), .clock(clock), .Load(Load), .clear(clear), .bus(bus), .Data_Out(Data_out),
    .Bus_Out(Bus_out));

  // Notes on the sheet:
  //   OLA 5
  //   ACC
  //   Diwas Dulal and Pujan Nepal
endmodule

module AR (
  input  clock,
  input  [31:0] Data_in,
  input  Load,
  output [31:0] Data_out
);

  Register register_1 (.Data_In(Data_in), .clock(clock), .Load(Load), .Data_Out(Data_out));

  // Notes on the sheet:
  //   OLA 5
  //   AR
  //   Diwas Dulal and Pujan Nepal
endmodule

module DR (
  input  clock,
  input  [31:0] Data_in,
  input  Load,
  input  bus,
  output [31:0] Data_out,
  output [31:0] Bus_out
);

  BusRegister busregister_1 (
    .Data_In(Data_in), .clock(clock), .Load(Load), .Bus(bus), .Data_Out(Data_out), .Bus_Out(Bus_out));

  // Notes on the sheet:
  //   OLA 5
  //   DR
  //   Diwas Dulal and Pujan Nepal
endmodule

module IR (
  input  clock,
  input  [31:0] Data_in,
  input  Load,
  output [31:0] Data_out
);

  Register register_1 (.Data_In(Data_in), .clock(clock), .Load(Load), .Data_Out(Data_out));

  // Notes on the sheet:
  //   OLA 5
  //   IR
  //   Diwas Dulal and Pujan Nepal
endmodule

module OUTR (
  input  clock,
  input  [31:0] Data_in,
  input  Load,
  output [31:0] Data_out
);

  Register register_1 (.Data_In(Data_in), .clock(clock), .Load(Load), .Data_Out(Data_out));

  // Notes on the sheet:
  //   OLA 5
  //   OUTR
  //   Diwas Dulal and Pujan Nepal
endmodule

module PC (
  input  clock,
  input  [31:0] Data_in,
  input  count,
  input  Load,
  input  bus,
  output [31:0] Data_out,
  output [31:0] Bus_out
);

  CountRegister countregister_1 (
    .Data_In(Data_in), .clock(clock), .count(count), .Load(Load), .bus(bus), .Data_Out(Data_out),
    .Bus_Out(Bus_out));

  // Notes on the sheet:
  //   OLA 5
  //   PC
  //   Diwas Dulal and Pujan Nepal
endmodule

module R (
  input  clock,
  input  [31:0] Data_in,
  input  Load,
  input  bus,
  output [31:0] Data_out,
  output [31:0] Bus_out
);

  BusRegister busregister_1 (
    .Data_In(Data_in), .clock(clock), .Load(Load), .Bus(bus), .Data_Out(Data_out), .Bus_Out(Bus_out));

  // Notes on the sheet:
  //   OLA 5
  //   R
  //   Diwas Dulal and Pujan Nepal
endmodule
